# Fritzing sketch CG3002 (saved by Fritzing 0.9.3b)
stripboards: 2

parts:
  Part1 = Arduino Mega 2560 (Rev3)
  Raspberry_Pi_2 = Raspberry Pi 3 [part_number=RPI-3-V1.2]
  Part5 = Logic Level Converter
  Part6 = INA169 Current Sensor Breakout [part_number=BOB-12040]
  R4 = Resistor [tolerance=±5% resistance=220 package="0402 [SMD]"]
  R5 = Resistor [tolerance=±5% resistance=220 package="0402 [SMD]"]
  BAT2 = Battery Holders [package=battery-aa]
  X2 = USB Connectors [package=usb-a-s-nosilk-female]
  X1 = USB Connectors [package=usb-a-s-nosilk-female]
  Part7 = InvenSense MPU6050
  Part8 = InvenSense MPU6050
  Part9 = InvenSense MPU6050

nets:
  N1: Part1.A0, Part6.VOUT
  N2: Part1.A1, R4.Pin_0, R5.Pin_1
  N3: Part1.D21/SCL, Part7.SCL, Part8.SCL, Part9.SCL
  N4: Part1.D20/SDA, Part7.SDA, Part8.SDA, Part9.SDA
  N5: Part1.D19/RX1, Part5.TX2_HV
  N6: Part1.D18/TX1, Part5.RX2_HV
  VCC: Part1.3V3, Part7.VCC, Part8.VCC, Part9.VCC
  GND: Part1.GND, Raspberry_Pi_2.GND, Part5.GND, Part7.GND, Part8.GND, Part9.GND
  N7: Part1.D2_PWM, Part7.AD0
  N8: Part1.D3_PWM, Part8.AD0
  N9: Part1.D4_PWM, Part9.AD0
  N10: Part1.5V, Part5.HV
  N11: Raspberry_Pi_2.3v3, Part5.LV
  N12: Raspberry_Pi_2.GIPO15, Part5.RX2_LV
  N13: Raspberry_Pi_2.GIPO14, Part5.TX2_LV
  GND_2: Part6.GND, R5.Pin_0, BAT2.+, X2.GND, X1.GND
  N14: Part6.VIN+, R4.Pin_1
  N15: Part6.VIN-, X2.VBUS, X1.VBUS
  N16: Part6.VCC, BAT2.-

custom parts:
  INA169 Current Sensor Breakout: INA169 Current Sensor Breakout Board
